# Fritzing sketch voice_light_circuit (saved by Fritzing 0.9.3b)
breadboards: 1

parts:
  Part1 = Arduino Uno (Rev3) - ICSP
  Mod1 = KY-019 5V Relay Module [package="Breakout board"]
  BULB1 = Incandescent light bulb small [package="bulb sm"]
  Part2 = Bluetooth HC-05 Macho

nets:
  GND: Part1.GND, Mod1.-, Part2.GND
  N1: Part1.D0/RX, Part2.TXD
  N2: Part1.D1/TX, Part2.RXD
  N3: Part1.D7, Mod1.S
  5V: Part1.5V, Mod1.+, Part2.VCC
  N4: Mod1.Common, BULB1.1

custom parts:
  KY-019 5V Relay Module: KY-019 5V Relay module, used to control AC circuits. (Special thanks to vanepp for fixing the PCB holes and other errors)
